// Logisim project experiment.circ as structural Verilog: 6 circuits, main circuit main
module main (
);


  // Notes on the sheet:
  //   电路仿真 —> 启用自动仿真√
  //   请先双击阅读左侧 参考器件及使用说明
  //   Window —> Preferences —> cn 切换中文
  //   电路仿真 —> 时钟连续√
endmodule

module _74160 (
  input  CLK,
  input  CLR,
  input  LE,
  input  CEP,
  input  CET,
  input  D1,
  input  D2,
  input  D3,
  input  D4,
  output Q1,
  output Q2,
  output Q3,
  output Q4,
  output TC
);

  wire and_1_out, and_2_out, and_3_out, and_4_out, and_5_out, and_6_out, and_7_out, and_8_out, and_9_out,
       and_10_out, and_11_out, and_12_out, and_13_out, d_ff_4_qn, not_1_out, not_2_out, or_1_out, or_2_out,
       or_3_out, or_4_out, or_5_out, xor_1_out, xor_2_out, xor_3_out, xor_4_out;

  not not_1 (not_1_out, CLR);
  and and_1 (and_1_out, LE, CEP, CET);
  not not_2 (not_2_out, LE);
  and and_2 (and_2_out, D1, not_2_out);
  and and_3 (and_3_out, Q1, LE);
  and and_4 (and_4_out, D2, not_2_out);
  and and_5 (and_5_out, Q2, LE);
  and and_6 (and_6_out, Q1, and_1_out, d_ff_4_qn);
  and and_7 (and_7_out, D3, not_2_out);
  and and_8 (and_8_out, Q3, LE);
  and and_9 (and_9_out, Q2, Q1, and_1_out);
  and and_10 (and_10_out, D4, not_2_out);
  and and_11 (and_11_out, Q4, LE);
  and and_12 (and_12_out, Q3, Q2, Q1, and_1_out);
  and and_13 (and_13_out, Q4, Q1, and_1_out);
  xor xor_1 (xor_1_out, and_3_out, and_1_out);
  xor xor_2 (xor_2_out, and_5_out, and_6_out);
  xor xor_3 (xor_3_out, and_8_out, and_9_out);
  or or_1 (or_1_out, and_12_out, and_13_out);
  or or_2 (or_2_out, and_2_out, xor_1_out);
  or or_3 (or_3_out, and_4_out, xor_2_out);
  or or_4 (or_4_out, and_7_out, xor_3_out);
  or or_5 (or_5_out, and_10_out, xor_4_out);
  xor xor_4 (xor_4_out, and_11_out, or_1_out);
  D_Flip_Flop #(.trigger("rising"), .Pre_Clr_Positions("ABOVE_BELOW"), .NegatePresetClear("false"), .enable("false"), .NewFFLayout("true")) d_ff_1 (
    .clk(CLK), .D(or_2_out), .Q(Q1), .reset(not_1_out));  // open: Qn, preset
  D_Flip_Flop #(.trigger("rising"), .Pre_Clr_Positions("ABOVE_BELOW"), .NegatePresetClear("false"), .enable("false"), .NewFFLayout("true")) d_ff_2 (
    .clk(CLK), .D(or_3_out), .Q(Q2), .reset(not_1_out));  // open: Qn, preset
  D_Flip_Flop #(.trigger("rising"), .Pre_Clr_Positions("ABOVE_BELOW"), .NegatePresetClear("false"), .enable("false"), .NewFFLayout("true")) d_ff_3 (
    .clk(CLK), .D(or_4_out), .Q(Q3), .reset(not_1_out));  // open: Qn, preset
  D_Flip_Flop #(.trigger("rising"), .Pre_Clr_Positions("ABOVE_BELOW"), .NegatePresetClear("false"), .enable("false"), .NewFFLayout("true")) d_ff_4 (
    .clk(CLK), .D(or_5_out), .Q(Q4), .Qn(d_ff_4_qn), .reset(not_1_out));  // open: preset
  and and_14 (TC, Q4, Q1, CET);
endmodule

module _74161 (
  input  CLK,
  input  CLR,
  input  LE,
  input  CEP,
  input  CET,
  input  D1,
  input  D2,
  input  D3,
  input  D4,
  output Q1,
  output Q2,
  output Q3,
  output Q4,
  output TC
);

  wire and_1_out, and_2_out, and_3_out, and_4_out, and_5_out, and_6_out, and_7_out, and_8_out, and_9_out,
       and_10_out, and_11_out, and_12_out, not_1_out, not_2_out, or_1_out, or_2_out, or_3_out, or_4_out,
       xor_1_out, xor_2_out, xor_3_out, xor_4_out;

  not not_1 (not_1_out, CLR);
  and and_1 (and_1_out, LE, CEP, CET);
  not not_2 (not_2_out, LE);
  and and_2 (and_2_out, D1, not_2_out);
  and and_3 (and_3_out, Q1, LE);
  and and_4 (and_4_out, D2, not_2_out);
  and and_5 (and_5_out, Q2, LE);
  and and_6 (and_6_out, Q1, and_1_out);
  and and_7 (and_7_out, D3, not_2_out);
  and and_8 (and_8_out, Q3, LE);
  and and_9 (and_9_out, Q2, Q1, and_1_out);
  and and_10 (and_10_out, D4, not_2_out);
  and and_11 (and_11_out, Q4, LE);
  and and_12 (and_12_out, Q3, Q2, Q1, and_1_out);
  xor xor_1 (xor_1_out, and_3_out, and_1_out);
  xor xor_2 (xor_2_out, and_5_out, and_6_out);
  xor xor_3 (xor_3_out, and_8_out, and_9_out);
  xor xor_4 (xor_4_out, and_11_out, and_12_out);
  or or_1 (or_1_out, and_2_out, xor_1_out);
  or or_2 (or_2_out, and_4_out, xor_2_out);
  or or_3 (or_3_out, and_7_out, xor_3_out);
  or or_4 (or_4_out, and_10_out, xor_4_out);
  D_Flip_Flop #(.trigger("rising"), .Pre_Clr_Positions("ABOVE_BELOW"), .NegatePresetClear("false"), .enable("false"), .NewFFLayout("true")) d_ff_1 (
    .clk(CLK), .D(or_1_out), .Q(Q1), .reset(not_1_out));  // open: Qn, preset
  D_Flip_Flop #(.trigger("rising"), .Pre_Clr_Positions("ABOVE_BELOW"), .NegatePresetClear("false"), .enable("false"), .NewFFLayout("true")) d_ff_2 (
    .clk(CLK), .D(or_2_out), .Q(Q2), .reset(not_1_out));  // open: Qn, preset
  D_Flip_Flop #(.trigger("rising"), .Pre_Clr_Positions("ABOVE_BELOW"), .NegatePresetClear("false"), .enable("false"), .NewFFLayout("true")) d_ff_3 (
    .clk(CLK), .D(or_3_out), .Q(Q3), .reset(not_1_out));  // open: Qn, preset
  D_Flip_Flop #(.trigger("rising"), .Pre_Clr_Positions("ABOVE_BELOW"), .NegatePresetClear("false"), .enable("false"), .NewFFLayout("true")) d_ff_4 (
    .clk(CLK), .D(or_4_out), .Q(Q4), .reset(not_1_out));  // open: Qn, preset
  and and_13 (TC, Q4, Q3, Q2, Q1, CET);
endmodule

// Hex2BCD
module \HEX2BCD_60以内  (
  input  D0,
  input  D1,
  input  D2,
  input  D3,
  input  D4,
  input  D5,
  input  D6,
  input  D7,
  output D0_2,
  output D1_2,
  output D2_2,
  output D3_2,
  output D4_2,
  output D5_2,
  output D6_2,
  output D7_2
);

  wire adder_1_cout, adder_2_cout, adder_3_cout, adder_4_cout, comparator_1_gt, comparator_2_gt,
       comparator_4_gt, comparator_5_gt, not_1_out, not_2_out;
  wire [2:0] and_1_out;
  wire [7:0] adder_1_out, adder_2_out, adder_3_out, adder_4_out, adder_5_out;

  Adder #(.width(8)) adder_1 (
    .a({D7, D6, D5, D4, D3, D2, D1, D0}), .b(8'h6), .out(adder_1_out), .cout(adder_1_cout));  // open: cin
  Adder #(.width(8)) adder_2 (
    .a({D7, D6, D5, D4, D3, D2, D1, D0}), .b(8'hc), .out(adder_2_out), .cin(adder_1_cout), .cout(adder_2_cout));
  Adder #(.width(8)) adder_3 (
    .a({D7, D6, D5, D4, D3, D2, D1, D0}), .b(8'h12), .out(adder_3_out), .cin(adder_2_cout),
    .cout(adder_3_cout));
  Adder #(.width(8)) adder_4 (
    .a({D7, D6, D5, D4, D3, D2, D1, D0}), .b(8'h18), .out(adder_4_out), .cin(adder_3_cout),
    .cout(adder_4_cout));
  Adder #(.width(8)) adder_5 (
    .a({D7, D6, D5, D4, D3, D2, D1, D0}), .b(8'h1e), .out(adder_5_out), .cin(adder_4_cout));  // open: cout
  Comparator #(.width(8), .mode("twosComplement")) comparator_1 (
    .a({D7, D6, D5, D4, D3, D2, D1, D0}), .b(8'h9), .gt(comparator_1_gt));  // open: eq, lt
  Comparator #(.width(8), .mode("twosComplement")) comparator_2 (
    .a({D7, D6, D5, D4, D3, D2, D1, D0}), .b(8'h13), .gt(comparator_2_gt));  // open: eq, lt
  Comparator #(.width(8), .mode("twosComplement")) comparator_3 (
    .a({D7, D6, D5, D4, D3, D2, D1, D0}), .b(8'h1d), .gt(and_1_out[2]));  // open: eq, lt
  not not_1 (not_1_out, comparator_4_gt);
  Comparator #(.width(8), .mode("twosComplement")) comparator_4 (
    .a({D7, D6, D5, D4, D3, D2, D1, D0}), .b(8'h27), .gt(comparator_4_gt));  // open: eq, lt
  not not_2 (not_2_out, comparator_5_gt);
  Comparator #(.width(8), .mode("twosComplement")) comparator_5 (
    .a({D7, D6, D5, D4, D3, D2, D1, D0}), .b(8'h31), .gt(comparator_5_gt));  // open: eq, lt
  Multiplexer #(.select(3), .width(8), .disabled(0), .enable("false")) multiplexer_1 (
    .in0({D7, D6, D5, D4, D3, D2, D1, D0}), .in1(adder_1_out), .in3(adder_2_out), .in4(adder_5_out),
    .in6(adder_4_out), .in7(adder_3_out), .out({D7_2, D6_2, D5_2, D4_2, D3_2, D2_2, D1_2, D0_2}),
    .sel(and_1_out));  // open: in2, in5
  and and_1 (and_1_out[0], comparator_1_gt, not_1_out);
  and and_2 (and_1_out[1], comparator_2_gt, not_2_out);
endmodule

module \参考器件及使用示例  (
  input  \逻辑输入_输出 ,
  output out_2
);

  wire button_1_out, clock_2_out, clock_3_out, displaydecoder_2_p2, displaydecoder_2_p3, displaydecoder_2_p4,
       displaydecoder_2_p5, displaydecoder_2_p6, displaydecoder_2_p7, displaydecoder_2_p8, \n7段译码器_2_a ,
       \n7段译码器_2_b , \n7段译码器_2_c , \n7段译码器_2_d , \n7段译码器_2_e , \n7段译码器_2_f , \n7段译码器_2_g , n74161_2_q1,
       n74161_2_q2, n74161_2_q3, n74161_2_q4;
  wire [3:0] counter_2_q, dipswitch_1_p2, n74160_2_q1;

  _74160 u_74160_1 ();  // open: CLK, CLR, LE, CEP, CET, D1, D2, D3, D4, Q1, Q2, Q3, Q4, TC
  _74161 u_74161_1 ();  // open: CLK, CLR, LE, CEP, CET, D1, D2, D3, D4, Q1, Q2, Q3, Q4, TC
  \_7段译码器  \u_7段译码器_1  ();  // open: A3, A2, A1, A0, a, b, c, d, e, f, g
  Clock #(.highDuration(1), .lowDuration(1)) clock_1 ();  // open: out
  \HEX2BCD_60以内  \Hex2BCD_60以内  ();  // open: D0, D1, D2, D3, D4, D5, D6, D7, D0_2, D1_2, D2_2, D3_2, D4_2, D5_2, D6_2, D7_2
  Clock #(.highDuration(1), .lowDuration(1)) clock_2 (.out(clock_2_out));
  D_Flip_Flop #(.trigger("rising"), .Pre_Clr_Positions("ABOVE_BELOW"), .NegatePresetClear("false"), .enable("false"), .NewFFLayout("true")) d_ff_1 ();  // open: clk, D, Q, Qn, preset, reset
  Counter #(.width(8), .max('hff), .ongoal("wrap"), .trigger("rising"), .behavior("new")) counter_1 ();  // open: load, D, count, Q, carry, clk, clr, preset, down
  J_K_Flip_Flop #(.trigger("rising"), .Pre_Clr_Positions("ABOVE_BELOW"), .NegatePresetClear("false"), .enable("false"), .NewFFLayout("true")) j_k_ff_1 ();  // open: J, clk, K, Q, Qn, preset, reset
  Shift_Register #(.width(1), .length(8), .parallel("true"), .trigger("rising")) shift_register_1 ();  // open: shift, in, clk, out, load, clr, d0, q0, d1, q1, d2, q2, d3, q3, d4, q4, d5, q5, d6, q6, d7, q7
  _74160 u_74160_2 (
    .CLK(clock_2_out), .CLR(1'b1), .LE(1'b1), .CEP(1'b1), .CET(1'b1), .D1(1'b0), .D2(1'b0), .D3(1'b0),
    .D4(1'b0), .Q1(n74160_2_q1[0]), .Q2(n74160_2_q1[1]), .Q3(n74160_2_q1[2]), .Q4(n74160_2_q1[3]));  // open: TC
  _74161 u_74161_2 (
    .CLK(clock_2_out), .CLR(1'b1), .LE(1'b1), .CEP(1'b1), .CET(1'b1), .D1(1'b0), .D2(1'b0), .D3(1'b0),
    .D4(1'b0), .Q1(n74161_2_q1), .Q2(n74161_2_q2), .Q3(n74161_2_q3), .Q4(n74161_2_q4));  // open: TC
  S_R_Flip_Flop #(.trigger("rising"), .Pre_Clr_Positions("ABOVE_BELOW"), .NegatePresetClear("false"), .enable("false"), .NewFFLayout("true")) s_r_ff_1 ();  // open: S, clk, R, Q, Qn, preset, reset
  Hex_Digit_Display hex_digit_display_1 (.value(n74160_2_q1));  // open: dp
  \_7段译码器  \u_7段译码器_2  (
    .A3(n74161_2_q4), .A2(n74161_2_q3), .A1(n74161_2_q2), .A0(n74161_2_q1), .a(\n7段译码器_2_a ),
    .b(\n7段译码器_2_b ), .c(\n7段译码器_2_c ), .d(\n7段译码器_2_d ), .e(\n7段译码器_2_e ), .f(\n7段译码器_2_f ), .g(\n7段译码器_2_g ));
  // NOT_Gate not_1 is placed but not wired
  // AND_Gate and_1 is placed but not wired
  // OR_Gate or_1 is placed but not wired
  // NAND_Gate nand_1 is placed but not wired
  // XNOR_Gate xnor_1 is placed but not wired
  Button button_1 (.out(button_1_out));
  _7_Segment_Display #(.active("true")) u_7_segment_display_1 (
    .g(\n7段译码器_2_g ), .f(\n7段译码器_2_f ), .a(\n7段译码器_2_a ), .b(\n7段译码器_2_b ), .e(\n7段译码器_2_e ),
    .d(\n7段译码器_2_d ), .c(\n7段译码器_2_c ));  // open: dp
  // NOR_Gate nor_1 is placed but not wired
  // XOR_Gate xor_1 is placed but not wired
  // Buzzer #(.freq_measure("Hz"), .vol_width(7)) buzzer_1: pin names not known; wires that end beside it: 14'h1f4, button_1_out, 7'b1100110
  // DisplayDecoder #(.multibit("true")) displaydecoder_1: pin names not known
  Clock #(.highDuration(1), .lowDuration(1)) clock_3 (.out(clock_3_out));
  Counter #(.width(4), .max('hf), .ongoal("wrap"), .trigger("rising"), .behavior("new")) counter_2 (
    .Q(counter_2_q), .clk(clock_3_out));  // open: load, D, count, carry, clr, preset, down
  // DipSwitch #(.NSwitches(4)) dipswitch_1: pin names not known; wires that end beside it: dipswitch_1_p2[1], dipswitch_1_p2[0], dipswitch_1_p2[2], dipswitch_1_p2[3]
  Button button_2 ();  // open: out
  // DipSwitch #(.NSwitches(4)) dipswitch_2: pin names not known
  // DisplayDecoder #(.multibit("true")) displaydecoder_2: pin names not known; wires that end beside it: counter_2_q, displaydecoder_2_p2, displaydecoder_2_p3, displaydecoder_2_p4, displaydecoder_2_p5, displaydecoder_2_p6, displaydecoder_2_p7, displaydecoder_2_p8
  LED #(.active("true")) led_1 (.in(dipswitch_1_p2[0]));
  // Switch #(.width(1)) switch_1: pin names not known
  Hex_Digit_Display hex_digit_display_2 (.value(dipswitch_1_p2));  // open: dp
  // Buzzer #(.freq_measure("Hz"), .vol_width(7)) buzzer_2: pin names not known
  LED #(.active("true")) led_2 ();  // open: in
  _7_Segment_Display #(.active("true")) u_7_segment_display_2 (
    .g(displaydecoder_2_p8), .f(displaydecoder_2_p7), .a(displaydecoder_2_p2), .b(displaydecoder_2_p3),
    .e(displaydecoder_2_p6), .d(displaydecoder_2_p5), .c(displaydecoder_2_p4));  // open: dp
  _7_Segment_Display #(.active("true")) u_7_segment_display_3 ();  // open: g, f, a, b, e, d, c, dp
  Hex_Digit_Display hex_digit_display_3 ();  // open: value, dp

  // Notes on the sheet:
  //   每个器件选中后，左下框图可选择不同属性
  //   器件的引脚，鼠标移到引脚处悬停会显示引脚说明。
  //   从左边库中拖出来即可使用，自定义封装时，仅需指定输入输出引脚
  //   线路/
  //   电源，逻辑1
  //   总线连接，示例为4位数据
  //   端口数和位宽可调节
  //   自建模型，从根目录直接拖动使用
  //   74160
  //   74161
  //   接地，逻辑0
  //   引脚属性，是否三态可选
  //   7段译码显示器
  //   时钟
  //   8位 2进制转10进制 60以内
  //   常量，可以表示0，1
  //   也可以表示多位
  //   标签，可指定位数
  //   一般与总线连接使用
  //   存储库/
  //   通用计数器
  //   74160，74161常规计数示例；数字直接显示示例；7段数码管译码后显示示例；
  //   D、JK、RS触发器
  //   通用移位寄存器
  //   逻辑门/
  //   复用器/
  //   通用7段译码显示器
  //   按钮+蜂鸣器示例
  //   输入输出/
  //   按钮，默认0，按下为1
  //   拨码开关
  //   通用计数器+通用7段译码显示器示例
  //   拨码开关与LED灯示例
  //   开关，需连接两端
  //   蜂鸣器
  //   需指定频率和音量
  //   Led灯
  //   7段数码管
  //   数字直接显示
endmodule

module \_7段译码器  (
  input  A0,
  input  A1,
  input  A2,
  input  A3,
  output a,
  output b,
  output c,
  output d,
  output e,
  output f,
  output g
);

  // DisplayDecoder #(.multibit("true")) displaydecoder_1: pin names not known; wires that end beside it: {A3, A2, A1, A0}, a, b, c, d, e, f, g
endmodule
